# Fritzing sketch electronic (saved by Fritzing 0.9.6b)
breadboards: 2

parts:
  Part1 = Arduino Uno (Rev3)
  Raspberry_Pi_1 = Raspberry Pi 3 [part_number=RPI-3-V1.2]
  DS1 = DS18B20 1-Wire Temperature Sensor [part_number=DS18B20]
  R1 = Resistor [tolerance=±5% power=0.25 resistance=220 package=THT]
  S1 = Round Pushbutton
  S2 = Round Pushbutton
  R4 = Resistor [tolerance=±5% power=0.25 resistance=220 package=THT]
  R5 = Resistor [tolerance=±5% power=0.25 resistance=220 package=THT]
  M1 = Stepper Motor - Bipolar
  DRV_1 = DRV 8825 Stepper Motor Carrier, High Current [part_number="DRV 8825"]
  C1 = Electrolytic Capacitor [capacitance=100µF voltage=35V package="200 mil [THT, electrolytic]"]
  Power_plug1 = Power plug
  S3 = Pushbutton [package=THT]
  S4 = Pushbutton [package=THT]
  R6 = Resistor [tolerance=±5% power=0.25 resistance=220 package=THT]
  R7 = Resistor [tolerance=±5% power=0.25 resistance=220 package=THT]

nets:
  N1: Part1.D8, DRV_1.DIRECTION
  N2: Part1.D9_PWM, DRV_1.STEP
  N3: Part1.D10_PWM/SS, DRV_1.MS1
  N4: Part1.D11_PWM/MOSI, DRV_1.MS2
  N5: Part1.D12/MISO, DRV_1.MS3
  N6: Part1.D13/SCK, DRV_1.SLEEP
  N7: Part1.D5_PWM, Raspberry_Pi_1.GPIO27
  N8: Part1.D6_PWM, S3.leg0, R7.Pin_1
  N9: Part1.D7, S4.leg0, R6.Pin_0
  N10: Part1.5V, DRV_1.RESET, R6.Pin_1, R7.Pin_0
  GND: Part1.GND, Raspberry_Pi_1.GND, DS1.GND, S1.leg0, S2.leg0, DRV_1.GROUND_LOG, C1.-, Power_plug1.GND, S3.leg1, S4.leg1
  3V3: Raspberry_Pi_1.3v3, DS1.VDD, R1.Pin_0
  N11: Raspberry_Pi_1.GPIO4, DS1.DQ, R1.Pin_1
  N12: Raspberry_Pi_1.GPIO17, S1.leg1, R4.Pin_0
  N13: Raspberry_Pi_1.GPIO18, S2.leg1, R5.Pin_0
  N14: Raspberry_Pi_1.5V, R4.Pin_1, R5.Pin_1
  N15: M1.A, DRV_1.OUT_2B
  N16: M1.C, DRV_1.OUT_2A
  N17: M1.B, DRV_1.OUT_1A
  N18: M1.D, DRV_1.OUT_1B
  N19: DRV_1.VOLTAGE_ST/_MT, C1.+, Power_plug1.VCC
